# Fritzing sketch Nigiri-schematic (saved by Fritzing 0.9.5d)

parts:
  Componente1 = LCD Keypad Shield  # not connected
  Componente3 = 16-Channel 12-bit PWM Servo Shield - I2C [part_number=1411]
  Componente4 = Arduino Uno (Rev3) - ICSP
  J1 = Basic Servo
  J2 = Basic Servo
  J3 = Basic Servo
  J4 = Basic Servo

nets:
  N1: Componente3.PWM3, J1.pulse
  VCC: Componente3.5.0V, J1.vcc, J2.vcc, J3.vcc, J4.vcc
  GND: Componente3.GND, J1.gnd, J2.gnd, J3.gnd, J4.gnd
  N2: Componente3.PWM2, J2.pulse
  N3: Componente3.PWM1, J3.pulse
  N4: Componente3.PWM0, J4.pulse
  N5: Componente3.SCL, Componente4.A5/SCL
  N6: Componente3.SDA, Componente4.A4/SDA

custom parts:
  LCD Keypad Shield: It consists of a 1602 white character blue backlight LCD. The keypad consists of 5 keys — select, up, right, down and left. To save the digital IO pins, the keypad interface uses only one ADC channel. The key value is read through a 5 stage voltage divider.
  16-Channel 12-bit PWM Servo Shield - I2C: You want to make a cool Arduino robot, maybe a hexapod walker, or maybe just a piece of art with a lot of moving parts. Or maybe you want to drive a lot of LEDs with precise PWM output. This shield is just like our popular PWM/Servo Breakout but now Arduino-ready and works with any Arduino that uses shields: Uno, Leo, Mega, ADK, its all good. Using only two I2C pins, control 16 free-running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
